# Fritzing sketch Sockets (saved by Fritzing 0.9.3b)

parts:
  Part1 = Arduino Uno (Rev3)
  U1 = 8RelayModule
  VCC_7+ = DC-DC CONVERTER [part_number=80633 package=dc-dc_converter]

nets:
  N1: Part1.A0, U1.IN5
  N2: Part1.A1, U1.IN6
  N3: Part1.A2, U1.IN7
  N4: Part1.A3, U1.IN8
  N5: Part1.D2, U1.IN4
  N6: Part1.D3_PWM, U1.IN3
  N7: Part1.D4, U1.IN2
  N8: Part1.D5_PWM, U1.IN1
  5V: Part1.5V, U1.VCC
  GND: Part1.GND, U1.GND, VCC_7+.OUT-
  N9: Part1.VIN, VCC_7+.OUT+

custom parts:
  8RelayModule: 8 relay arduino module SONGLE SRD05VDC-SL-C
  DC-DC CONVERTER: WYHP 5A constant current/voltage manufactured by Shenzhen Weiyapuhua Technology Co., Ltd
